// Logisim project andor_gate.circ as structural Verilog
module main (
  input  in_1,
  input  in_2,
  input  in_3,
  input  in_4,
  output out_5,
  output out_6
);

  gate4 gate4_1 (.a(in_1), .b(in_2), .c(in_3), .d(in_4), .out1(out_5), .out2(out_6));
endmodule

// VHDL entity gate4, as the project stores it:
library IEEE;
use IEEE.STD_LOGIC_1164.ALL;

entity gate4 is
    port (
        a, b, c, d : in  STD_LOGIC;
        out1       : out STD_LOGIC;
        out2       : out STD_LOGIC
    );
end gate4;

architecture Behavioral of gate4 is
begin
    out1 <= a and b and c and d;
    out2 <= a or b or c or d;
end Behavioral;
